// Logisim project computer.circ as structural Verilog
module addsub_4bit (
  input  cin,
  input  [3:0] A,
  input  [3:0] B,
  input  sub,
  output [3:0] S,
  output [3:0] F
);

  wire adder_1_cout, adder_2_cout, adder_3_cout, xor_1_out, xor_2_out, xor_3_out, xor_4_out, xor_5_out;

  xor xor_1 (xor_1_out, cin, sub);
  xor xor_2 (xor_2_out, B[0], sub);
  xor xor_3 (xor_3_out, B[1], sub);
  xor xor_4 (xor_4_out, B[2], sub);
  xor xor_5 (xor_5_out, B[3], sub);
  Adder #(.width(1)) adder_1 (.a(A[0]), .b(xor_2_out), .out(S[0]), .cin(xor_1_out), .cout(adder_1_cout));
  Adder #(.width(1)) adder_2 (.a(A[1]), .b(xor_3_out), .out(S[1]), .cin(adder_1_cout), .cout(adder_2_cout));
  Adder #(.width(1)) adder_3 (.a(A[2]), .b(xor_4_out), .out(S[2]), .cin(adder_2_cout), .cout(adder_3_cout));
  Adder #(.width(1)) adder_4 (.a(A[3]), .b(xor_5_out), .out(F[1]), .cin(adder_3_cout), .cout(F[2]));
  and and_1 (F[0], ~S[0], ~S[1], ~S[2], ~F[1]);  // AND_Gate
  xor xor_6 (F[3], adder_3_cout, F[2]);

  assign S[3] = F[1];
endmodule

module addsub_4bit_test (
);

  wire dipswitch_2_sw1, dipswitch_4_sw1;
  wire [3:0] addsub_4bit_1_f, addsub_4bit_1_s, dipswitch_1_sw1, dipswitch_3_sw1;

  DipSwitch #(.number(4)) dipswitch_1 (
    .sw1(dipswitch_1_sw1[0]), .sw2(dipswitch_1_sw1[1]), .sw3(dipswitch_1_sw1[2]), .sw4(dipswitch_1_sw1[3]));
  DipSwitch #(.number(1)) dipswitch_2 (.sw1(dipswitch_2_sw1));
  DipSwitch #(.number(4)) dipswitch_3 (
    .sw1(dipswitch_3_sw1[0]), .sw2(dipswitch_3_sw1[1]), .sw3(dipswitch_3_sw1[2]), .sw4(dipswitch_3_sw1[3]));
  DipSwitch #(.number(1)) dipswitch_4 (.sw1(dipswitch_4_sw1));
  addsub_4bit addsub_4bit_1 (
    .cin(dipswitch_2_sw1), .A(dipswitch_1_sw1), .B(dipswitch_3_sw1), .sub(dipswitch_4_sw1),
    .S(addsub_4bit_1_s), .F(addsub_4bit_1_f));
  LedBar ledbar_1 (
    .led0(addsub_4bit_1_s[0]), .led1(addsub_4bit_1_s[1]), .led2(addsub_4bit_1_s[2]),
    .led3(addsub_4bit_1_s[3]), .led4(addsub_4bit_1_f[0]), .led5(addsub_4bit_1_f[1]),
    .led6(addsub_4bit_1_f[2]), .led7(addsub_4bit_1_f[3]));
endmodule

module full_adder (
  input  A,
  input  B,
  input  Cin,
  output S,
  output Cout
);

  wire and_1_out, and_2_out, xor_1_out;

  and and_1 (and_1_out, A, B);
  xor xor_1 (xor_1_out, A, B);
  xor xor_2 (S, xor_1_out, Cin);
  and and_2 (and_2_out, xor_1_out, Cin);
  or or_1 (Cout, and_2_out, and_1_out);
endmodule
